// Logisim project tennis.circ as structural Verilog: 6 circuits, main circuit main
module main (
);

  wire [4:0] controller_1_out_2, controller_1_out_3, controller_1_out_4, controller_1_out_5,
       controller_1_out_6, display_1_out_14, display_1_out_15, display_1_out_16, display_1_out_17,
       display_1_out_18, display_2_out_14, display_2_out_15, display_2_out_16, display_2_out_17,
       display_2_out_18, display_3_out_14, display_3_out_15, display_3_out_16, display_3_out_17,
       display_3_out_18;
  wire [31:0] undriven, undriven_2, undriven_3, undriven_4, undriven_5, undriven_6, undriven_7, undriven_8,
       undriven_9, undriven_10, undriven_11, undriven_12, undriven_13, undriven_14, undriven_15, undriven_16,
       undriven_17, undriven_18, undriven_19, undriven_20, undriven_21, undriven_22, undriven_23,
       undriven_24, undriven_25, undriven_26, undriven_27, undriven_28, undriven_29, undriven_30,
       undriven_31, undriven_32;

  _7_Segment_Display u_7_segment_display_1 ();  // open: g, f, a, b, e, d, c, dp
  DotMatrix #(.matrixcols(32), .matrixrows(32)) dotmatrix_1 (
    .col0(undriven), .col1(undriven_2), .col2(undriven_3), .col3(undriven_4), .col4(undriven_5),
    .col5(undriven_6), .col6(undriven_7), .col7(undriven_8), .col8(undriven_9), .col9(undriven_10),
    .col10(undriven_11), .col11(undriven_12), .col12(undriven_13), .col13(undriven_14), .col14(undriven_15),
    .col15(undriven_16), .col16(undriven_17), .col17(undriven_18), .col18(undriven_19), .col19(undriven_20),
    .col20(undriven_21), .col21(undriven_22), .col22(undriven_23), .col23(undriven_24), .col24(undriven_25),
    .col25(undriven_26), .col26(undriven_27), .col27(undriven_28), .col28(undriven_29), .col29(undriven_30),
    .col30(undriven_31), .col31(undriven_32));
  controller controller_1 (
    .out_2(controller_1_out_2), .out_3(controller_1_out_3), .out_4(controller_1_out_4),
    .out_5(controller_1_out_5), .out_6(controller_1_out_6));  // open: in_1
  display display_1 (
    .in_9(controller_1_out_2), .in_10(controller_1_out_3), .in_11(controller_1_out_4),
    .in_12(controller_1_out_5), .in_13(controller_1_out_6), .out_14(display_1_out_14),
    .out_15(display_1_out_15), .out_16(display_1_out_16), .out_17(display_1_out_17),
    .out_18(display_1_out_18), .in_3(undriven), .in_1(undriven_2), .in_2(undriven_3), .in_4(undriven_4),
    .in_5(undriven_5), .in_6(undriven_6), .in_7(undriven_7), .in_8(undriven_8));
  display display_2 (
    .in_9(display_1_out_14), .in_10(display_1_out_15), .in_11(display_1_out_16), .in_12(display_1_out_17),
    .in_13(display_1_out_18), .out_14(display_2_out_14), .out_15(display_2_out_15),
    .out_16(display_2_out_16), .out_17(display_2_out_17), .out_18(display_2_out_18), .in_3(undriven_9),
    .in_1(undriven_10), .in_2(undriven_11), .in_4(undriven_12), .in_5(undriven_13), .in_6(undriven_14),
    .in_7(undriven_15), .in_8(undriven_16));
  display display_3 (
    .in_9(display_2_out_14), .in_10(display_2_out_15), .in_11(display_2_out_16), .in_12(display_2_out_17),
    .in_13(display_2_out_18), .out_14(display_3_out_14), .out_15(display_3_out_15),
    .out_16(display_3_out_16), .out_17(display_3_out_17), .out_18(display_3_out_18), .in_3(undriven_17),
    .in_1(undriven_18), .in_2(undriven_19), .in_4(undriven_20), .in_5(undriven_21), .in_6(undriven_22),
    .in_7(undriven_23), .in_8(undriven_24));
  _7_Segment_Display u_7_segment_display_2 ();  // open: g, f, a, b, e, d, c, dp
  display display_4 (
    .in_9(display_3_out_14), .in_10(display_3_out_15), .in_11(display_3_out_16), .in_12(display_3_out_17),
    .in_13(display_3_out_18), .in_3(undriven_25), .in_1(undriven_26), .in_2(undriven_27), .in_4(undriven_28),
    .in_5(undriven_29), .in_6(undriven_30), .in_7(undriven_31), .in_8(undriven_32));  // open: out_14, out_15, out_16, out_17, out_18
endmodule

module inc (
  input  [4:0] in_1,
  output [4:0] out_2
);

  Adder #(.width(5)) adder_1 (.a(in_1), .b(5'b00001), .out(out_2));  // open: cin, cout
endmodule

module display (
  input  [31:0] in_1,
  input  [31:0] in_2,
  input  [31:0] in_3,
  input  [31:0] in_4,
  input  [31:0] in_5,
  input  [31:0] in_6,
  input  [31:0] in_7,
  input  [31:0] in_8,
  input  [4:0] in_9,
  input  [4:0] in_10,
  input  [4:0] in_11,
  input  [4:0] in_12,
  input  [4:0] in_13,
  output [4:0] out_14,
  output [4:0] out_15,
  output [4:0] out_16,
  output [4:0] out_17,
  output [4:0] out_18
);

  wire comparator_1_eq;

  assign in_2 = {{31{1'b0}}, comparator_1_eq};  // Bit_Extender bit_extender_1
  Comparator #(.width(5)) comparator_1 (.a(in_9), .b({5{1'b0}}), .eq(comparator_1_eq));  // open: gt, lt
  inc inc_1 (.in_1(in_9), .out_2(out_14));

  assign out_15 = in_10;
  assign out_16 = in_11;
  assign out_17 = in_12;
  assign out_18 = in_13;
endmodule

module controller (
  input  in_1,
  output [4:0] out_2,
  output [4:0] out_3,
  output [4:0] out_4,
  output [4:0] out_5,
  output [4:0] out_6
);

  wire clock;
  wire [2:0] motion_1_new_speed, motion_2_new_speed, vx_q, vy_q;
  wire [4:0] x_q, y_q;

  Clock clock_1 (.out(clock));
  Register #(.width(3)) vy (.D(motion_2_new_speed), .Q(vy_q), .clk(clock));  // open: en, clr
  Register #(.width(3)) vx (.D(motion_1_new_speed), .Q(vx_q), .clk(clock));  // open: en, clr
  Register #(.width(5)) x (.D(out_2), .Q(x_q), .clk(clock));  // open: en, clr
  motion motion_1 (.in_1(x_q), .speed(vx_q), .new_cords(out_2), .new_speed(motion_1_new_speed));
  Register #(.width(5)) y (.D(out_6), .Q(y_q), .clk(clock));  // open: en, clr
  motion motion_2 (.in_1(y_q), .speed(vy_q), .new_cords(out_6), .new_speed(motion_2_new_speed));
  Multiplexer #(.width(5)) multiplexer_1 ();  // open: in0, in1, out, sel, en

  assign out_3 = {5{1'b0}};

  // Other names for the same wires on the sheet: reset = in_1
endmodule

module reflect (
  input  [2:0] speed,
  input  cout,
  output [2:0] out_3,
  output out_4
);

  wire [2:0] negator_1_out;

  Negator #(.width(3)) negator_1 (.in(speed), .out(negator_1_out));
  xor xor_1 (out_4, speed[2], cout);
  Multiplexer #(.width(3)) multiplexer_1 (.in0(speed), .in1(negator_1_out), .out(out_3), .sel(out_4));  // open: en
endmodule

module motion (
  input  [4:0] in_1,
  input  [2:0] speed,
  output [4:0] new_cords,
  output [2:0] new_speed
);

  wire adder_1_cout, reflect_1_out_4;
  wire [4:0] adder_1_out, bit_extender_1_out;

  assign bit_extender_1_out = {{2{1'b0}}, speed};  // Bit_Extender bit_extender_1
  Adder #(.width(5)) adder_1 (.a(in_1), .b(bit_extender_1_out), .out(adder_1_out), .cout(adder_1_cout));  // open: cin
  reflect reflect_1 (.speed(speed), .cout(adder_1_cout), .out_3(new_speed), .out_4(reflect_1_out_4));
  Multiplexer #(.width(5)) multiplexer_1 (
    .in0(adder_1_out), .in1(in_1), .out(new_cords), .sel(reflect_1_out_4));  // open: en
  // also tied to GND on the sheet: adder_1_cout
endmodule
